# Fritzing sketch schematic (saved by Fritzing 0.9.4)
breadboards: 1

parts:
  M1 = Stepper Motor - Bipolar
  Pololu_A1 = Pololu A4988 [package=SO16]
  Raspberry_Pi_1 = Raspberry Pi 3 [part_number=RPI-3-V1.2]
  C2 = Electrolytic Capacitor [capacitance=47µF voltage=16V package="300 mil [THT, electrolytic]"]
  JACK1 = 2.1mm Barrel Jack with Terminal Block
  Mod1 = KY-024 Linear Hall Magnetic Sensor Module [package="Breakout board"]
  KY-1 = Keyes Relay [package=THT]
  LED1 = LEDs [package=led10mm]

nets:
  N1: M1.A, Pololu_A1.2B
  N2: M1.C, Pololu_A1.2A
  N3: M1.B, Pololu_A1.1A
  N4: M1.D, Pololu_A1.1B
  N5: Pololu_A1.ENABLE, Raspberry_Pi_1.GIPO16
  N6: Pololu_A1.RESET, Pololu_A1.SLEEP
  N7: Pololu_A1.STEP, Raspberry_Pi_1.GIPO20
  N8: Pololu_A1.DIR, Raspberry_Pi_1.GIPO21
  N9: Pololu_A1.GND#8, Raspberry_Pi_1.GND, Mod1.G, KY-1.ground
  3V3: Pololu_A1.VDD, Raspberry_Pi_1.3v3, Raspberry_Pi_1.3V3, Mod1.+
  N10: Pololu_A1.GND#14, C2.-, JACK1.NEG
  N11: Pololu_A1.VMOT, C2.+, JACK1.POS
  N12: Raspberry_Pi_1.GIPO6, KY-1.signal
  N13: Raspberry_Pi_1.GIPO26, Mod1.D0
  N14: Raspberry_Pi_1.5V, KY-1.power
  N15: KY-1.NC, LED1.C

custom parts:
  KY-024 Linear Hall Magnetic Sensor Module: KY-024 Linear Hall Magnetic Sensor Module reacts iin the presence of a magnetic field.
  Keyes Relay: The Keyes 5V relay module is suitable for SCM development, home appliance control. It uses a 5V~12V TIL control signal which can control DC / AC signal.
